// Logisim project stack_logical_normal.circ as structural Verilog: 15 circuits, main circuit main
module main (
  input  CLK,
  input  RESET,
  input  [1:0] COMMAND,
  input  [2:0] INDEX,
  input  [3:0] IO_DATA_in,
  output [3:0] IO_DATA_out
);

  stack stack_1 (
    .CLK(CLK), .RESET(RESET), .COMMAND(COMMAND), .INDEX(INDEX), .IO_DATA_in(IO_DATA_in),
    .IO_DATA_out(IO_DATA_out));
endmodule

module stack (
  input  CLK,
  input  RESET,
  input  [1:0] COMMAND,
  input  [2:0] INDEX,
  input  [3:0] IO_DATA_in,
  output [3:0] IO_DATA_out
);

  wire and_1_out, and_2_out, and_3_out, C, last_index_2_out_c, mem_index_1_out_c, mem_index_2_out_c,
       next_index_2_out_c, not_1_out, not_2_out, not_3_out, not_u_3_out_2, not_u_4_out_2, or_1_out, or_2_out,
       r, xor_1_out;
  wire [2:0] index_get_1_out_4, index_t, last_index_1_index_last, last_index_2_index_last,
       mem_index_1_out_index, mem_index_2_out_index, mux2_2_out_4, mux2_3_out_4, next_index_1_index_next,
       next_index_2_index_next;
  wire [3:0] memory_1_outdata;

  not_u not_u_1 (.in_1(CLK), .out_2(C));
  not_u not_u_2 (.in_1(RESET), .out_2(r));
  not_u not_u_3 (.in_1(COMMAND[1]), .out_2(not_u_3_out_2));
  not_u not_u_4 (.in_1(COMMAND[0]), .out_2(not_u_4_out_2));
  and and_1 (and_1_out, C, ~not_u_3_out_2, not_u_4_out_2);  // AND_Gate
  and and_2 (and_2_out, C, not_u_3_out_2, ~not_u_4_out_2);  // AND_Gate
  and and_3 (and_3_out, C, not_u_3_out_2, not_u_4_out_2);
  xor xor_1 (xor_1_out, not_u_3_out_2, not_u_4_out_2);
  not not_1 (not_1_out, not_u_4_out_2);
  mem_index mem_index_1 (
    .Reset(r), .C(or_2_out), .in_index(mux2_3_out_4), .out_index(mem_index_1_out_index),
    .out_c(mem_index_1_out_c));
  not not_2 (not_2_out, mem_index_1_out_c);
  index_get index_get_1 (.c(and_3_out), .head_index(index_t), .get_index(INDEX), .out_4(index_get_1_out_4));
  mux2 mux2_1 (.in1(mux2_3_out_4), .num(not_1_out), .in2(mem_index_2_out_index), .out_4(index_t));
  mem_index mem_index_2 (
    .Reset(r), .C(not_2_out), .in_index(mem_index_1_out_index), .out_index(mem_index_2_out_index),
    .out_c(mem_index_2_out_c));
  mux2 mux2_2 (.in1(index_get_1_out_4), .num(xor_1_out), .in2(index_t), .out_4(mux2_2_out_4));
  next_index next_index_1 (
    .index(mem_index_2_out_index), .c(mem_index_2_out_c), .index_next(next_index_1_index_next));  // open: out_c
  or or_1 (or_1_out, and_1_out, ~C, r);  // OR_Gate
  last_index last_index_1 (
    .index(mem_index_2_out_index), .c(mem_index_2_out_c), .index_last(last_index_1_index_last));  // open: out_c
  memory memory_1 (.data(IO_DATA_in), .index(mux2_2_out_4), .num(and_1_out), .reset(r), .outdata(memory_1_outdata));
  not not_3 (not_3_out, or_1_out);
  next_index next_index_2 (
    .index(last_index_1_index_last), .c(and_1_out), .out_c(next_index_2_out_c),
    .index_next(next_index_2_index_next));
  last_index last_index_2 (
    .index(next_index_1_index_next), .c(and_2_out), .out_c(last_index_2_out_c),
    .index_last(last_index_2_index_last));
  Transistor #(.width(4)) transistor_1 (.in(memory_1_outdata), .out(IO_DATA_in), .gate(or_1_out));
  Transistor #(.\type ("n"), .width(4)) transistor_2 (.in(memory_1_outdata), .out(IO_DATA_in), .gate(not_3_out));
  or or_2 (or_2_out, next_index_2_out_c, last_index_2_out_c);
  mux2 mux2_3 (.in1(next_index_2_index_next), .num(not_u_4_out_2), .in2(last_index_2_index_last), .out_4(mux2_3_out_4));

  assign IO_DATA_out = IO_DATA_in;

  // Other names for the same wires on the sheet: idata[3:0] = IO_DATA_in

  // Notes on the sheet:
  //   your circuit must be here
endmodule

module next_index (
  input  [2:0] index,
  input  c,
  output out_c,
  output [2:0] index_next
);

  wire and_1_out, and_2_out, and_3_out, and_4_out, and_5_out, and_6_out, and_7_out, and_8_out, and_9_out,
       nand_1_out, not_1_out, xor_1_out, xor_2_out;

  and and_1 (and_1_out, index[1], index[0]);
  not not_1 (not_1_out, index[0]);
  xor xor_1 (xor_1_out, index[2], and_1_out);
  xor xor_2 (xor_2_out, index[1], index[0]);
  nand nand_1 (nand_1_out, xor_1_out, not_1_out);
  and and_2 (and_2_out, xor_1_out, nand_1_out);
  and and_3 (and_3_out, and_2_out, c);
  and and_4 (and_4_out, xor_2_out, c);
  and and_5 (and_5_out, nand_1_out, not_1_out);
  and and_6 (and_6_out, and_5_out, c);
  and and_7 (and_7_out, index[2], ~c);  // AND_Gate
  or or_1 (index_next[2], and_3_out, and_7_out);
  and and_8 (and_8_out, index[1], ~c);  // AND_Gate
  or or_2 (index_next[1], and_4_out, and_8_out);
  or or_3 (index_next[0], and_6_out, and_9_out);
  and and_9 (and_9_out, index[0], ~c);  // AND_Gate

  assign out_c = c;
endmodule

module last_index (
  input  [2:0] index,
  input  c,
  output out_c,
  output [2:0] index_last
);

  wire and_1_out, and_2_out, and_3_out, and_4_out, and_5_out, and_6_out, and_7_out, and_8_out, nand_1_out,
       nor_1_out, not_1_out, xnor_1_out, xor_1_out;

  nor nor_1 (nor_1_out, index[1], index[0]);
  xnor xnor_1 (xnor_1_out, index[1], index[0]);
  not not_1 (not_1_out, index[0]);
  xor xor_1 (xor_1_out, index[2], nor_1_out);
  nand nand_1 (nand_1_out, xor_1_out, not_1_out);
  and and_1 (and_1_out, nand_1_out, not_1_out);
  and and_2 (and_2_out, nand_1_out, xnor_1_out);
  and and_3 (and_3_out, xor_1_out, c);
  and and_4 (and_4_out, and_2_out, c);
  and and_5 (and_5_out, and_1_out, c);
  and and_6 (and_6_out, index[2], ~c);  // AND_Gate
  and and_7 (and_7_out, index[1], ~c);  // AND_Gate
  and and_8 (and_8_out, index[0], ~c);  // AND_Gate
  or or_1 (index_last[2], and_3_out, and_6_out);
  or or_2 (index_last[1], and_4_out, and_7_out);
  or or_3 (index_last[0], and_5_out, and_8_out);

  assign out_c = c;
endmodule

module index_get (
  input  c,
  input  [2:0] head_index,
  input  [2:0] get_index,
  output [2:0] out_4
);

  wire and_1_out, and_2_out, and_3_out, and_4_out, and_5_out, not_1_out, not_2_out, not_3_out, or_1_out,
       or_2_out, xor_1_out, xor_2_out, xor_3_out, xor_4_out, xor_5_out;
  wire [2:0] last_index_1_index_last;
  wire [3:0] and_9_out;

  last_index last_index_1 (.index(head_index), .c(c), .index_last(last_index_1_index_last));  // open: out_c
  xor xor_1 (xor_1_out, get_index[2], or_1_out);
  and and_1 (and_1_out, or_1_out, get_index[2]);
  xor xor_2 (xor_2_out, last_index_1_index_last[1], xor_3_out);
  xor xor_3 (xor_3_out, get_index[1], and_4_out);
  and and_2 (and_2_out, get_index[1], and_4_out);
  not not_1 (not_1_out, last_index_1_index_last[0]);
  not not_2 (not_2_out, last_index_1_index_last[2]);
  not not_3 (not_3_out, last_index_1_index_last[1]);
  and and_3 (and_3_out, not_3_out, xor_3_out);
  or or_1 (or_1_out, and_3_out, and_2_out);
  and and_4 (and_4_out, not_1_out, get_index[0]);
  xor xor_4 (xor_4_out, last_index_1_index_last[0], get_index[0]);
  xor xor_5 (xor_5_out, last_index_1_index_last[2], xor_1_out);
  and and_5 (and_5_out, xor_1_out, not_2_out);
  or or_2 (or_2_out, and_1_out, and_5_out);
  and and_6 (and_9_out[3], or_2_out, c);
  and and_7 (and_9_out[2], c, xor_5_out);
  and and_8 (and_9_out[1], c, xor_2_out);
  and and_9 (and_9_out[0], c, xor_4_out);
  mod_for_index mod_for_index_1 (.IN4(and_9_out), .OUT3(out_4));
endmodule

module mod_for_index (
  input  [3:0] IN4,
  output [2:0] OUT3
);

  wire and_1_out, and_2_out, and_3_out, and_4_out, and_5_out, and_6_out, and_7_out, and_8_out, and_9_out,
       and_10_out, and_11_out, and_12_out, mex3_1_out0, mex3_1_out1, mex3_1_out2, mex3_2_out0, mex3_2_out1,
       mex3_2_out2, mex3_3_out0, mex3_3_out1, mex3_3_out2, mex3_4_out0, mex3_4_out1, mex3_4_out2,
       mex3_5_out0, mex3_5_out1, mex3_5_out2, not_1_out, not_2_out, not_3_out, not_4_out, not_5_out,
       not_6_out, not_7_out, not_8_out, not_9_out, or_1_out, or_2_out, or_3_out, or_4_out, or_5_out;

  not not_1 (not_1_out, IN4[3]);
  not not_2 (not_2_out, IN4[2]);
  not not_3 (not_3_out, IN4[1]);
  not not_4 (not_4_out, IN4[0]);
  and and_1 (and_1_out, not_1_out, not_2_out, not_3_out, not_4_out);
  and and_2 (and_2_out, IN4[3], not_2_out, IN4[1], IN4[0]);
  and and_3 (and_3_out, not_1_out, not_2_out, not_2_out, IN4[0]);
  and and_4 (and_4_out, IN4[3], IN4[2], not_3_out, not_4_out);
  and and_5 (and_5_out, not_1_out, not_2_out, IN4[1], not_4_out);
  and and_6 (and_6_out, IN4[3], IN4[2], not_3_out, IN4[0]);
  and and_7 (and_7_out, not_1_out, not_2_out, IN4[1], IN4[0]);
  and and_8 (and_8_out, IN4[3], IN4[2], IN4[1], not_4_out);
  and and_9 (and_9_out, not_1_out, IN4[2], not_3_out, not_4_out);
  and and_10 (and_10_out, IN4[3], IN4[2], IN4[1], IN4[0]);
  and and_11 (and_11_out, IN4[3], not_2_out, not_3_out, IN4[0]);
  and and_12 (and_12_out, IN4[3], not_2_out, IN4[1], not_4_out);
  or or_1 (or_1_out, and_1_out, and_2_out);
  or or_2 (or_2_out, and_3_out, and_4_out);
  or or_3 (or_3_out, and_5_out, and_6_out);
  or or_4 (or_4_out, and_7_out, and_11_out, and_8_out);
  or or_5 (or_5_out, and_9_out, and_12_out, and_10_out);
  not not_5 (not_5_out, or_1_out);
  not not_6 (not_6_out, or_2_out);
  not not_7 (not_7_out, or_3_out);
  not not_8 (not_8_out, or_4_out);
  not not_9 (not_9_out, or_5_out);
  mex3 mex3_1 (
    .IN0(not_5_out), .IN1(not_5_out), .IN2(not_5_out), .C(or_1_out), .OUT0(mex3_1_out0), .OUT1(mex3_1_out1),
    .OUT2(mex3_1_out2));
  mex3 mex3_2 (
    .IN0(not_6_out), .IN1(not_6_out), .IN2(or_2_out), .C(or_2_out), .OUT0(mex3_2_out0), .OUT1(mex3_2_out1),
    .OUT2(mex3_2_out2));
  mex3 mex3_3 (
    .IN0(not_7_out), .IN1(or_3_out), .IN2(not_7_out), .C(or_3_out), .OUT0(mex3_3_out0), .OUT1(mex3_3_out1),
    .OUT2(mex3_3_out2));
  mex3 mex3_4 (
    .IN0(not_8_out), .IN1(or_4_out), .IN2(or_4_out), .C(or_4_out), .OUT0(mex3_4_out0), .OUT1(mex3_4_out1),
    .OUT2(mex3_4_out2));
  mex3 mex3_5 (
    .IN0(or_5_out), .IN1(not_9_out), .IN2(not_9_out), .C(or_5_out), .OUT0(mex3_5_out0), .OUT1(mex3_5_out1),
    .OUT2(mex3_5_out2));
  or or_6 (OUT3[2], mex3_1_out0, mex3_2_out0, mex3_3_out0, mex3_4_out0, mex3_5_out0);
  or or_7 (OUT3[1], mex3_1_out1, mex3_2_out1, mex3_3_out1, mex3_4_out1, mex3_5_out1);
  or or_8 (OUT3[0], mex3_1_out2, mex3_2_out2, mex3_3_out2, mex3_4_out2, mex3_5_out2);
endmodule

module mex3 (
  input  IN0,
  input  IN1,
  input  IN2,
  input  C,
  output OUT0,
  output OUT1,
  output OUT2
);

  and and_1 (OUT0, IN0, C);
  and and_2 (OUT1, IN1, C);
  and and_3 (OUT2, IN2, C);
endmodule

module memory_cell (
  input  [3:0] Change,
  input  Command,
  input  Reset,
  output [3:0] Read
);

  wire and_1_out, and_2_out, and_3_out, and_4_out, xor_1_out;

  and and_1 (and_1_out, Change[3], ~Reset);  // AND_Gate
  xor xor_1 (xor_1_out, Command, Reset);
  and and_2 (and_2_out, Change[2], ~Reset);  // AND_Gate
  and and_3 (and_3_out, Change[1], ~Reset);  // AND_Gate
  and and_4 (and_4_out, Change[0], ~Reset);  // AND_Gate
  D d_1 (.S(and_1_out), .C(xor_1_out), .Q(Read[3]));
  D d_2 (.S(and_2_out), .C(xor_1_out), .Q(Read[2]));
  D d_3 (.S(and_3_out), .C(xor_1_out), .Q(Read[1]));
  D d_4 (.S(and_4_out), .C(xor_1_out), .Q(Read[0]));
endmodule

module D (
  input  S,
  input  C,
  output Q
);

  wire and_1_out, and_2_out, nor_2_out, not_1_out;

  not not_1 (not_1_out, S);
  and and_1 (and_1_out, not_1_out, C);
  and and_2 (and_2_out, C, S);
  nor nor_1 (Q, and_1_out, nor_2_out);
  nor nor_2 (nor_2_out, Q, and_2_out);
endmodule

module mem_index (
  input  Reset,
  input  C,
  input  [2:0] in_index,
  output [2:0] out_index,
  output out_c
);

  wire or_1_out;
  wire [2:0] and_1_out;

  or or_1 (or_1_out, Reset, C);
  assign and_1_out = ~{3{Reset}} & in_index;  // AND_Gate and_1, 3 bits wide
  D d_1 (.S(and_1_out[2]), .C(or_1_out), .Q(out_index[2]));
  D d_2 (.S(and_1_out[1]), .C(or_1_out), .Q(out_index[1]));
  D d_3 (.S(and_1_out[0]), .C(or_1_out), .Q(out_index[0]));

  assign out_c = C;
endmodule

module MEX (
  input  [2:0] index,
  input  num,
  output out1,
  output out2,
  output out3,
  output out4,
  output out5
);

  wire and_1_out, and_2_out, and_3_out, and_4_out, and_5_out;

  and and_1 (and_1_out, ~index[2], ~index[1], ~index[0]);  // AND_Gate
  and and_2 (and_2_out, ~index[2], ~index[1], index[0]);  // AND_Gate
  and and_3 (and_3_out, ~index[2], index[1], ~index[0]);  // AND_Gate
  and and_4 (and_4_out, ~index[2], index[1], index[0]);  // AND_Gate
  and and_5 (and_5_out, index[2], ~index[1], ~index[0]);  // AND_Gate
  and and_6 (out1, and_1_out, num);
  and and_7 (out2, and_2_out, num);
  and and_8 (out3, and_3_out, num);
  and and_9 (out4, and_4_out, num);
  and and_10 (out5, and_5_out, num);
endmodule

module MUX (
  input  [3:0] in0,
  input  [3:0] in1,
  input  [3:0] in2,
  input  [3:0] in3,
  input  [3:0] in4,
  input  [2:0] index,
  output [3:0] outdata
);

  wire [3:0] and_6_out, and_7_out, and_8_out, and_9_out, and_10_out;
  wire [3:3] and_1_out, and_2_out, and_3_out, and_4_out, and_5_out;

  and and_1 (and_1_out[3], ~index[2], ~index[1], ~index[0]);  // AND_Gate
  and and_2 (and_2_out[3], ~index[2], ~index[1], index[0]);  // AND_Gate
  and and_3 (and_3_out[3], ~index[2], index[1], ~index[0]);  // AND_Gate
  and and_4 (and_4_out[3], ~index[2], index[1], index[0]);  // AND_Gate
  and and_5 (and_5_out[3], index[2], ~index[1], ~index[0]);  // AND_Gate
  assign and_6_out = in0 & {4{and_1_out[3]}};  // AND_Gate and_6, 4 bits wide
  assign and_7_out = in1 & {4{and_2_out[3]}};  // AND_Gate and_7, 4 bits wide
  assign and_8_out = in2 & {4{and_3_out[3]}};  // AND_Gate and_8, 4 bits wide
  assign and_9_out = in3 & {4{and_4_out[3]}};  // AND_Gate and_9, 4 bits wide
  assign and_10_out = in4 & {4{and_5_out[3]}};  // AND_Gate and_10, 4 bits wide
  ExactlyOne xor_1[3:0] (
    .out(outdata), .in0(and_6_out), .in1(and_7_out), .in2(and_8_out), .in3(and_9_out), .in4(and_10_out));
endmodule

module mux2 (
  input  [2:0] in1,
  input  num,
  input  [2:0] in2,
  output [2:0] out_4
);

  wire [2:0] and_1_out, and_2_out;

  assign and_1_out = in1 & {3{num}};  // AND_Gate and_1, 3 bits wide
  assign and_2_out = ~{3{num}} & in2;  // AND_Gate and_2, 3 bits wide
  assign out_4 = and_1_out ^ and_2_out;  // XOR_Gate xor_1, 3 bits wide
endmodule

module memory (
  input  [3:0] data,
  input  [2:0] index,
  input  num,
  input  reset,
  output [3:0] outdata
);

  wire mex_1_out1, mex_1_out2, mex_1_out3, mex_1_out4, mex_1_out5;
  wire [3:0] memory_cell_1_read, memory_cell_2_read, memory_cell_3_read, memory_cell_4_read,
       memory_cell_5_read;

  MEX mex_1 (
    .index(index), .num(num), .out1(mex_1_out1), .out2(mex_1_out2), .out3(mex_1_out3), .out4(mex_1_out4),
    .out5(mex_1_out5));
  memory_cell memory_cell_1 (.Change(data), .Command(mex_1_out1), .Reset(reset), .Read(memory_cell_1_read));
  memory_cell memory_cell_2 (.Change(data), .Command(mex_1_out2), .Reset(reset), .Read(memory_cell_2_read));
  memory_cell memory_cell_3 (.Change(data), .Command(mex_1_out3), .Reset(reset), .Read(memory_cell_3_read));
  memory_cell memory_cell_4 (.Change(data), .Command(mex_1_out4), .Reset(reset), .Read(memory_cell_4_read));
  memory_cell memory_cell_5 (.Change(data), .Command(mex_1_out5), .Reset(reset), .Read(memory_cell_5_read));
  MUX mux_1 (
    .in0(memory_cell_1_read), .in1(memory_cell_2_read), .in2(memory_cell_3_read), .in3(memory_cell_4_read),
    .in4(memory_cell_5_read), .index(index), .outdata(outdata));

  // Other names for the same wires on the sheet: idata[3:0] = data
endmodule

module not_u (
  input  in_1,
  output out_2
);


  assign out_2 = in_1;
endmodule
